# Fritzing sketch Hosseini (saved by Fritzing 0.9.3b)
breadboards: 1

parts:
  IC1 = IC, DIP package, 8 pins [chip_label=IC]
  R1 = Resistor [tolerance=±5% resistance=470 package=THT]
  LED1 = LED - 5mm [color="Red (633nm)" package="5 mm [THT]"]
  D1 = Zener Diode [part_number=1N4732A breakdown_voltage=3.6V package="Melf DO-213 AB [SMD]"]
  R2 = Photocell (LDR) [package=THT]
  R3 = Resistor [tolerance=±5% resistance=3.3k package=THT]
  R4 = Resistor [tolerance=±5% resistance=4.7k package=THT]
  VCC1 = Battery block 9V

nets:
  N1: IC1.pin2, D1.cathode, R3.Pin_1
  N2: IC1.pin3, R4.Pin_0
  GND: IC1.pin4, LED1.cathode, D1.anode, R4.Pin_1, VCC1.-
  N3: IC1.pin6, R1.Pin_0
  N4: IC1.pin7, R2.pin_0, R3.Pin_0, VCC1.+
  N5: R1.Pin_1, LED1.anode
